# Fritzing sketch sensor (saved by Fritzing 0.9.2b)
stripboards: 2

parts:
  part = ESP8266 WiFi Module [part_number=ESP8266-ESP12]
  D1 = Schottky Diode [package="300 mil [THT]"]
  SOIL = female pin header, 4 pins [form="♀ (female)"]
  DHT11 = female pin header, 3 pins [form="♀ (female)"]
  3xAA_NIMH = female pin header, 2 pins [form="♀ (female)"]
  SOLAR = female pin header, 2 pins [form="♀ (female)"]
  Q1 = PNP-Transistor [package="TO92 [THT]"]
  D2 = Zener Diode [breakdown_voltage=3.9V package="300 mil [THT]"]
  R2 = Resistor [tolerance=±5% resistance=33k package=THT]
  R3 = Resistor [tolerance=±5% resistance=66k package=THT]
  R6 = Resistor [tolerance=±5% resistance=1k package=THT]
  R5 = Resistor [tolerance=±5% resistance=10k package=THT]

nets:
  N1: part.VCC, D1.cathode, 3xAA_NIMH.pin1, Q1.E, D2.cathode, R5.Pin_0
  N2: part.GND, SOIL.pin2, DHT11.pin3, 3xAA_NIMH.pin2, SOLAR.pin2, D2.anode, R3.Pin_1
  N3: part.GPIO_4, DHT11.pin2
  N4: part.ADC_0, R2.Pin_1, R3.Pin_0
  N5: part.GPIO_12, R6.Pin_1, R5.Pin_1
  N6: D1.anode, SOLAR.pin1
  N7: SOIL.pin1, DHT11.pin1, Q1.C
  N8: SOIL.pin4, R2.Pin_0
  N9: Q1.B, R6.Pin_0

custom parts:
  ESP8266 WiFi Module: Mini ESP8266 Breakout Board
